# Fritzing sketch thermo (saved by Fritzing 0.9.3b)
breadboards: 1

parts:
  LCD1 = LCD screen
  R4 = Resistor [tolerance=±5% resistance=220 package=THT]
  R5 = Temperature Sensor (Thermistor) [thermistor_type=NTC package=THT]
  R6 = Trimmer Potentiometer [maximum_resistance=10kΩ package=THT]
  Part1 = Arduino Uno (Rev3)

nets:
  VSS: LCD1.VSS, LCD1.R/W, LCD1.LED-, R4.Pin_1, R6.leg2, Part1.GND
  VDD: LCD1.VDD, LCD1.LED+, R5.pin_1, R6.leg1, Part1.5V
  N1: LCD1.V0, R6.wiper
  N2: LCD1.RS, Part1.D7
  N3: LCD1.E, Part1.D8
  N4: LCD1.DB4, Part1.D9_PWM
  N5: LCD1.DB5, Part1.D10_PWM/SS
  N6: LCD1.DB6, Part1.D11_PWM/MOSI
  N7: LCD1.DB7, Part1.D12/MISO
  N8: R4.Pin_0, R5.pin_0, Part1.A0
